# Fritzing sketch 00-Rpi-i2c-ATMEGA_connectionConcept (saved by Fritzing 0.9.3b)
breadboards: 2

parts:
  Raspberry_Pi_1 = Raspberry Pi 3 [part_number=RPI-3-V1.2]
  Componente1 = Arduino Uno (Rev3) - ICSP
  U1 = atmega328 [package=dip]

nets:
  N1: Raspberry_Pi_1.GPIO2, Componente1.A4/SDA, U1.A4
  N2: Raspberry_Pi_1.GPIO3, Componente1.A5/SCL, U1.A5
  GND: Raspberry_Pi_1.GND, Componente1.GND, U1.GND#7

notes:
  CONEXIÓN I2C - VARIOS DISPOSITIVOS
  RaspberryPi ----> I2C MASTER
  ATMEGA328P ----> I2C SLAVE
  ARDUINO UNO ----> I2C SLAVE
