# Fritzing sketch 2-ATMEGA_to_RPI_CUADRO (saved by Fritzing 0.9.3b)
breadboards: 1

parts:
  Raspberry_Pi_2 = Raspberry Pi 3 [part_number=RPI-3-V1.2]
  U4 = atmega328 [package=dip]
  J16 = female pin header, 2 pins [form="♀ (female)"]
  J17 = female pin header, 2 pins [form="♀ (female)"]
  J18 = female pin header, 2 pins [form="♀ (female)"]
  J19 = female pin header, 2 pins [form="♀ (female)"]
  J20 = female pin header, 2 pins [form="♀ (female)"]
  J21 = female pin header, 2 pins [form="♀ (female)"]
  J22 = female pin header, 2 pins [form="♀ (female)"]
  J23 = female pin header, 2 pins [form="♀ (female)"]
  J24 = female pin header, 2 pins [form="♀ (female)"]
  J25 = female pin header, 2 pins [form="♀ (female)"]
  KY-7 = Keyes Relay [package=THT]
  KY-8 = Keyes Relay [package=THT]
  KY-9 = Keyes Relay [package=THT]
  KY-10 = Keyes Relay [package=THT]
  KY-11 = Keyes Relay [package=THT]
  U5 = OPTO_DARL_6N138S [package=8-smd]
  U6 = OPTO_DARL_6N138S [package=8-smd]
  KY-12 = Keyes Relay [package=THT]
  13-15 = Screw terminal - 2 pins [package=THT]  # not connected
  25-27 = Screw terminal - 2 pins [package=THT]
  27-29 = Screw terminal - 2 pins [package=THT]
  15-17 = Screw terminal - 2 pins [package=THT]  # not connected
  17-19 = Screw terminal - 2 pins [package=THT]  # not connected
  29-31 = Screw terminal - 2 pins [package=THT]
  31-33 = Screw terminal - 2 pins [package=THT]
  19-21 = Screw terminal - 2 pins [package=THT]  # not connected
  3-5 = Screw terminal - 2 pins [package=THT]
  7-9 = Screw terminal - 2 pins [package=THT]
  1-3 = Screw terminal - 2 pins [package=THT]
  21-23 = Screw terminal - 2 pins [package=THT]  # not connected
  23-25 = Screw terminal - 2 pins [package=THT]  # not connected
  5-7 = Screw terminal - 2 pins [package=THT]
  9-11 = Screw terminal - 2 pins [package=THT]  # not connected
  33-35 = Screw terminal - 2 pins [package=THT]
  11-13 = Screw terminal - 2 pins [package=THT]  # not connected

nets:
  N1: Raspberry_Pi_2.GPIO2, U4.A4, J25.pin2
  N2: Raspberry_Pi_2.GPIO3, U4.A5, J25.pin1
  N3: Raspberry_Pi_2.GND, U4.GND#7, J16.pin1, J16.pin2, KY-7.ground, KY-8.ground, KY-9.ground, KY-10.ground, KY-11.ground, KY-12.ground
  5V: Raspberry_Pi_2.5V, U4.VCC, J17.pin1, J17.pin2, KY-7.power, KY-8.power, KY-9.power, KY-10.power, KY-11.power, KY-12.power
  N4: U4.RESET, J19.pin1
  N5: U4.D0_(RX), J18.pin1, J19.pin2
  N6: U4.D1_(TX), J18.pin2
  N7: U4.D9_(PWM), U4.D12, U4.AREF, J20.pin2, J22.pin2, KY-8.signal
  N8: U4.D10_(PWM), U4.D13, U4.GND#21, J20.pin1, J21.pin2, J22.pin1, KY-10.signal, KY-12.signal
  N9: U4.D11_(PWM), U4.AVCC, J21.pin1, KY-11.signal
  N10: U4.A0, J23.pin2, KY-9.signal
  N11: U4.A1, J23.pin1, KY-7.signal
  N12: U4.A2, J24.pin2, U6.VOUT
  N13: U4.A3, J24.pin1, U5.VOUT
  N14: KY-7.NO, KY-8.NC, KY-8.C, KY-10.C, KY-11.C, KY-12.C, 7-9.pin2
  N15: KY-8.NO, 3-5.pin2
  N16: KY-9.NO, 25-27.pin2
  N17: KY-10.NO, 1-3.pin2
  N18: KY-11.NO, 1-3.pin1
  N19: U5.A, 5-7.pin1
  N20: U5.C, U6.C
  GND: U5.GND, U6.GND
  VCC: U5.VCC, U6.VCC
  N21: U6.A, 5-7.pin2
  N22: KY-12.NO, 3-5.pin1
  N23: 25-27.pin1, 29-31.pin2, 31-33.pin1
  N24: 27-29.pin2, 29-31.pin1, 33-35.pin2

notes:
  ATMEGA328P ----> I2C SLAVE
  RaspberryPi ----> I2C MASTER
  ATMEGA a RaspberryPi Y ELEMENTOS DEL CUADRO y BOX
  ---------------------------------------------------------------------------------------------------
  24v to 5v
  -------------
  GND >
  +5V >
  RELE con:
  220v to 24v
  o
  24V del controlador
  ---------------------------
  GND >
  +24V >
  Cerradura
  Led
  Verde
  Led
  Amarillo
  Led
  Rojo
  Enchufe
  Cargador
  BOX
  ON/OFF
  BOX
  Relé con:
  Del Inversor
  o
  De la General
  220V~ 50Hz
  L1 N T
  ENCHUFEs
  Sensor
  Puerta
  Sensor
  Patineta
  optoacopladores
  ATMEGA-PinOUT Ref.
  RPI-PinOUT Ref.

custom parts:
  Keyes Relay: The Keyes 5V relay module is suitable for SCM development, home appliance control. It uses a 5V~12V TIL control signal which can control DC / AC signal.
