# Fritzing sketch 3-BOX_Connection_to_Cuadro (saved by Fritzing 0.9.3b)
breadboards: 1

parts:
  1-2 = Screw terminal - 2 pins [package=THT]
  3-4 = Screw terminal - 2 pins [package=THT]
  5-6 = Screw terminal - 2 pins [package=THT]
  7-8 = Screw terminal - 2 pins [package=THT]
  9-10 = Screw terminal - 2 pins [package=THT]
  11-12 = Screw terminal - 2 pins [package=THT]  # not connected
  SENSOR_PATINETA = Infrared Proximity Sensor
  ELECTROIMÁN_(Cerradura) = DC Motor
  SENSOR_PUERTA = Infrared Proximity Sensor
  13-15 = Screw terminal - 2 pins [package=THT]  # not connected
  25-27 = Screw terminal - 2 pins [package=THT]  # not connected
  27-29 = Screw terminal - 2 pins [package=THT]
  15-17 = Screw terminal - 2 pins [package=THT]  # not connected
  17-19 = Screw terminal - 2 pins [package=THT]  # not connected
  29-31 = Screw terminal - 2 pins [package=THT]  # not connected
  31-33 = Screw terminal - 2 pins [package=THT]  # not connected
  19-21 = Screw terminal - 2 pins [package=THT]  # not connected
  3-5 = Screw terminal - 2 pins [package=THT]
  7-9 = Screw terminal - 2 pins [package=THT]
  1-3 = Screw terminal - 2 pins [package=THT]
  21-23 = Screw terminal - 2 pins [package=THT]  # not connected
  23-25 = Screw terminal - 2 pins [package=THT]  # not connected
  5-7 = Screw terminal - 2 pins [package=THT]
  9-11 = Screw terminal - 2 pins [package=THT]
  33-35 = Screw terminal - 2 pins [package=THT]  # not connected
  11-13 = Screw terminal - 2 pins [package=THT]  # not connected
  LED1 = smd LED [color="Green (560nm)" package="0603 [SMD]"]
  LED2 = smd LED [color="Yellow (595nm)" package="0603 [SMD]"]
  LED3 = smd LED [color="Red (633nm)" package="0603 [SMD]"]

nets:
  N1: 1-2.pin1, 1-3.pin2, LED1.anode
  N2: 1-2.pin2, 1-3.pin1, LED2.anode
  N3: 3-4.pin1, 3-5.pin2, LED3.anode
  N4: 3-4.pin2, ELECTROIMÁN_(Cerradura).pin_1, 3-5.pin1
  N5: 5-6.pin1, 5-7.pin2
  N6: 5-6.pin2, 5-7.pin1
  N7: 7-8.pin1, SENSOR_PATINETA.Vcc, 7-9.pin2
  GND: 7-8.pin2, 9-10.pin1, 9-10.pin2, SENSOR_PATINETA.GND, ELECTROIMÁN_(Cerradura).pin_2, SENSOR_PUERTA.GND, 7-9.pin1, 9-11.pin2, LED1.cathode, LED2.cathode, LED3.cathode
  N8: 27-29.pin1, 27-29.pin2

notes:
  230V~ (ALTERNA)
  [ENCHUFE-CARGADOR]
  L1 N (T)
  24V - (CONTINUA)
  (imaginación)
  SENSOR PATINETA
  (imaginación)
  SENSOR PUERTA
  (imaginación)
  ELECTROIMÁN (cerradura)
  LED VERDE
  (Disponible)
  LED AMARILLO
  (Reservado)
  LED ROJO
  (Ocupado)
  ****LEYENDA****
  #################################
  //////////////////////////////////////////////////////////
  SENSORES -DETECTORES (Puerta/Patineta) (PNP)
  -------------------------------------------------------------------
  MARRON: POSITIVO (24V)
  AZUL: NEGATIVO (0V)
  NEGRO: DATA -> INPUT ATMEGA (Optoacopl.)
  =======================================
  //////////////////////////////////////////////////////////
  ELECTROIMÁN (Cerradura)
  -------------------------------------------------------------------
  NEGRO: NEGATIVO (0V)
  NARANJA: IN(+)<- OUTPUT ATMEGA (Relé)
  =======================================
  //////////////////////////////////////////////////////////
  LEDS (Verde,Amarillo,Rojo)
  -------------------------------------------------------------------NEGRO: NEGATIVO (0V)
  VERDE: IN(+)<-OUTPUT ATMEGA (Relé)
  AMARILLO: IN(+)<-OUTPUT ATMEGA (Relé)
  ROJO: IN(+)<-OUTPUT ATMEGA (Relé)
  =======================================
  BOX BLUECITY-ATMEGA
